// Digital circuit DMux8Way16.dig as structural Verilog
module DMux8Way16 (
  input  In,
  input  sel0,
  input  sel1,
  input  sel2,
  output a,
  output b,
  output c,
  output d,
  output e,
  output f,
  output g,
  output h
);

  wire chip_dmux_1_a, chip_dmux_1_b;

  chip_DMux chip_dmux_1 (.sel(sel0), .in(In), .A(chip_dmux_1_a), .B(chip_dmux_1_b));
  chip_DMux4Way chip_dmux4way_1 (.sel_0(sel1), .sel_1(sel2), .In(chip_dmux_1_a), .A(a), .B(b), .C(c), .D(d));
  chip_DMux4Way chip_dmux4way_2 (.sel_0(sel1), .sel_1(sel2), .In(chip_dmux_1_b), .A(e), .B(f), .C(g), .D(h));
endmodule
