// Digital circuit Mux4Way16.dig as structural Verilog
module Mux4Way16 (
  input  a,
  input  b,
  input  c,
  input  d,
  input  S1,
  input  S0,
  output o
);

  wire chip_mux_1_o, chip_mux_2_o;

  chip_Mux chip_mux_1 (.a(a), .b(b), .S(S0), .o(chip_mux_1_o));
  chip_Mux chip_mux_2 (.a(c), .b(d), .S(S0), .o(chip_mux_2_o));
  chip_Mux chip_mux_3 (.a(chip_mux_1_o), .b(chip_mux_2_o), .S(S1), .o(o));
endmodule
