// Digital circuit Mux8Way16.dig as structural Verilog
module Mux8Way16 (
  input  a,
  input  b,
  input  c,
  input  d,
  input  e,
  input  f,
  input  g,
  input  h,
  input  S0,
  input  S1,
  input  S2,
  output out_12
);

  wire mux4way16_1_o, mux4way16_2_o;

  Mux4Way16 mux4way16_1 (.a(a), .b(b), .c(c), .d(d), .S1(S1), .S0(S0), .o(mux4way16_1_o));
  Mux4Way16 mux4way16_2 (.a(e), .b(f), .c(g), .d(h), .S1(S0), .S0(S1), .o(mux4way16_2_o));
  chip_Mux chip_mux_1 (.a(mux4way16_1_o), .b(mux4way16_2_o), .S(S2), .o(out_12));
endmodule
