// Digital circuit chip_And.dig as structural Verilog
module chip_And (
  input  a,
  input  b,
  output o
);

  wire nand_1_out;

  nand nand_1 (nand_1_out, a, b);
  chip_Not chip_not_1 (.in(nand_1_out), .out(o));
endmodule
