// Digital circuit chip_DMux.dig as structural Verilog
module chip_DMux (
  input  sel,
  input  in,
  output A,
  output B
);

  wire chip_not_1_out;

  chip_Not chip_not_1 (.in(sel), .out(chip_not_1_out));
  chip_And chip_and_1 (.a(in), .b(chip_not_1_out), .o(A));
  chip_And chip_and_2 (.a(sel), .b(in), .o(B));
endmodule
