// Digital circuit chip_DMux4Way.dig as structural Verilog
module chip_DMux4Way (
  input  sel_0,
  input  sel_1,
  input  In,
  output A,
  output B,
  output C,
  output D
);

  wire chip_dmux_1_a, chip_dmux_1_b;

  chip_DMux chip_dmux_1 (.sel(sel_0), .in(In), .A(chip_dmux_1_a), .B(chip_dmux_1_b));
  chip_DMux chip_dmux_2 (.sel(sel_1), .in(chip_dmux_1_a), .A(A), .B(B));
  chip_DMux chip_dmux_3 (.sel(sel_1), .in(chip_dmux_1_b), .A(C), .B(D));
endmodule
