// Digital circuit chip_Mux.dig as structural Verilog
module chip_Mux (
  input  a,
  input  b,
  input  S,
  output o
);

  wire chip_and_1_o, chip_and_2_o, chip_not_1_out;

  chip_Not chip_not_1 (.in(S), .out(chip_not_1_out));
  chip_And chip_and_1 (.a(a), .b(chip_not_1_out), .o(chip_and_1_o));
  chip_And chip_and_2 (.a(S), .b(b), .o(chip_and_2_o));
  chip_Or chip_or_1 (.a(chip_and_1_o), .b(chip_and_2_o), .o(o));
endmodule
