// Digital circuit chip_Or.dig as structural Verilog
module chip_Or (
  input  a,
  input  b,
  output o
);

  wire not_1_out, not_2_out;

  not not_1 (not_1_out, a);
  not not_2 (not_2_out, b);
  nand nand_1 (o, not_1_out, not_2_out);
endmodule
