// Digital circuit chip_Xor.dig as structural Verilog
module chip_Xor (
  input  a,
  input  b,
  output o
);

  wire chip_and_1_o, chip_and_2_o, chip_not_1_out, chip_not_2_out;

  chip_Not chip_not_1 (.in(a), .out(chip_not_1_out));
  chip_Not chip_not_2 (.in(b), .out(chip_not_2_out));
  chip_And chip_and_1 (.a(chip_not_1_out), .b(b), .o(chip_and_1_o));
  chip_And chip_and_2 (.a(a), .b(chip_not_2_out), .o(chip_and_2_o));
  chip_Or chip_or_1 (.a(chip_and_1_o), .b(chip_and_2_o), .o(o));
endmodule
