// Digital circuit 16bit_adder.dig as structural Verilog
module _16bit_adder (
  input  a0,
  input  b0,
  input  a1,
  input  b1,
  input  in_7,
  input  a2,
  input  b2,
  output o_0,
  output o_1,
  output o_2
);

  wire full_adder_1_carry, full_adder_2_carry;

  full_adder full_adder_1 (.a(a0), .b(b0), .c(in_7), .carry(full_adder_1_carry), .sum(o_0));
  full_adder full_adder_2 (.a(a1), .b(b1), .c(full_adder_1_carry), .carry(full_adder_2_carry), .sum(o_1));
  full_adder full_adder_3 (.a(a2), .b(b2), .c(full_adder_2_carry), .sum(o_2));  // open: carry
endmodule
