// Digital circuit Clock_not_here.dig as structural Verilog
module Clock_not_here (
  input  in,
  input  inc,
  input  load,
  input  reset,
  input  _000_address,
  input  inc_chip,
  output out_7
);

  wire multiplexer_1_out, multiplexer_2_out, multiplexer_3_out;

  Multiplexer multiplexer_1 (.sel(load), .in_0(multiplexer_3_out), .in_1(in), .out(multiplexer_1_out));
  Multiplexer multiplexer_2 (.sel(reset), .in_0(multiplexer_1_out), .in_1(_000_address), .out(multiplexer_2_out));
  Multiplexer multiplexer_3 (.sel(inc), .in_0(multiplexer_2_out), .in_1(inc_chip), .out(multiplexer_3_out));
  and and_1 (out_7, multiplexer_3_out, multiplexer_3_out);
endmodule
