// Digital circuit full_adder.dig as structural Verilog
module full_adder (
  input  a,
  input  b,
  input  c,
  output carry,
  output sum
);

  wire and_1_out, half_adder_1_carry, half_adder_1_sum, half_adder_2_carry, half_adder_2_sum,
       half_adder_3_carry, or_1_out, or_3_out;

  half_adder half_adder_1 (.a(a), .b(b), .sum(half_adder_1_sum), .carry(half_adder_1_carry));
  half_adder half_adder_2 (.a(a), .b(c), .sum(half_adder_2_sum), .carry(half_adder_2_carry));
  half_adder half_adder_3 (.a(b), .b(c), .carry(half_adder_3_carry));  // open: sum
  or or_1 (or_1_out, half_adder_1_carry, half_adder_2_carry);
  or or_2 (carry, or_1_out, half_adder_3_carry);
  and and_1 (and_1_out, half_adder_1_sum, half_adder_2_sum);
  or or_3 (or_3_out, and_1_out, half_adder_1_sum);
  xor xor_1 (sum, or_3_out, c);
endmodule
