// Digital circuit incrementor.dig as structural Verilog
module incrementor (
  input  in_0,
  input  inc,
  input  in_2,
  input  in_3,
  input  in_8,
  output o_0,
  output o_1,
  output o_2
);

  _16bit_adder _16bit_adder_1 (
    .a0(in_0), .b0(inc), .a1(in_2), .b1(in_8), .in_7(in_8), .a2(in_3), .b2(in_8), .o_0(o_0), .o_1(o_1),
    .o_2(o_2));
endmodule
