// Digital circuit inspirations.dig as structural Verilog
module inspirations (
  input  a,
  input  b,
  input  c,
  input  d,
  input  e,
  input  f,
  output carry,
  output sum,
  output out_9
);

  wire and_1_out, and_2_out, and_3_out, half_adder_1_carry, half_adder_1_sum, half_adder_2_carry,
       half_adder_2_sum, half_adder_3_carry, half_adder_4_sum, half_adder_5_sum, or_1_out, or_3_out,
       or_4_out, xor_1_out, xor_2_out;

  half_adder half_adder_1 (.a(a), .b(b), .sum(half_adder_1_sum), .carry(half_adder_1_carry));
  half_adder half_adder_2 (.a(a), .b(c), .sum(half_adder_2_sum), .carry(half_adder_2_carry));
  half_adder half_adder_3 (.a(b), .b(c), .carry(half_adder_3_carry));  // open: sum
  xor xor_1 (xor_1_out, d, e);
  xor xor_2 (xor_2_out, d, e);
  or or_1 (or_1_out, half_adder_1_carry, half_adder_2_carry);
  or or_2 (carry, or_1_out, half_adder_3_carry);
  and and_1 (and_1_out, xor_1_out, xor_2_out);
  and and_2 (and_2_out, half_adder_1_sum, half_adder_2_sum);
  or or_3 (or_3_out, and_1_out, xor_2_out);
  or or_4 (or_4_out, and_2_out, half_adder_1_sum);
  xor xor_3 (out_9, or_3_out, f);
  half_adder half_adder_4 (.a(or_4_out), .b(c), .sum(half_adder_4_sum));  // open: carry
  half_adder half_adder_5 (.a(or_4_out), .b(c), .sum(half_adder_5_sum));  // open: carry
  and and_3 (and_3_out, half_adder_4_sum, half_adder_5_sum);
  or or_5 (sum, and_3_out, half_adder_4_sum);
endmodule
