// Digital circuit Jumps.dig as structural Verilog
module Jumps (
  input  ng,
  input  zr,
  output J3,
  output J2,
  output J1
);

  wire not_1_out, not_2_out;

  not not_1 (not_1_out, ng);
  not not_2 (not_2_out, zr);
  and and_1 (J3, not_1_out, not_2_out);

  assign J1 = ng;
  assign J2 = zr;
endmodule
