// Digital circuit Logic_after_jump.dig as structural Verilog
module Logic_after_jump (
  input  ng,
  input  zr,
  output JGT,
  output JEQ,
  output JGE,
  output out_6
);

  wire jumps_1_j1;

  Jumps jumps_1 (.ng(ng), .zr(zr), .J3(JGT), .J2(JEQ), .J1(jumps_1_j1));
  and and_1 (JGE, JEQ, jumps_1_j1);
endmodule
