// Digital circuit Logic_jmp_cpu.dig as structural Verilog
module Logic_jmp_cpu (
  input  J1,
  input  J2,
  input  J3,
  input  Positive,
  input  ng,
  input  zr,
  input  none,
  input  all,
  output out_7
);

  wire and_1_out, and_2_out, and_3_out, and_4_out, and_5_out, and_6_out, and_7_out, and_8_out, and_9_out,
       and_10_out, not_1_out, or_1_out, or_2_out, or_3_out, or_4_out;

  or or_1 (or_1_out, zr, ng);
  or or_2 (or_2_out, zr, Positive);
  or or_3 (or_3_out, zr, Positive);
  and and_1 (and_1_out, J3, J2);
  and and_2 (and_2_out, J3, J1);
  and and_3 (and_3_out, J2, J1);
  and and_4 (and_4_out, ng, J1);
  and and_5 (and_5_out, or_3_out, and_1_out);
  and and_6 (and_6_out, Positive, J3);
  and and_7 (and_7_out, zr, J2);
  and and_8 (and_8_out, or_2_out, and_2_out);
  and and_9 (and_9_out, or_1_out, and_3_out);
  or or_4 (or_4_out, and_4_out, and_5_out, and_6_out, and_7_out, and_8_out, and_9_out);
  and and_10 (and_10_out, not_1_out, or_4_out);
  not not_1 (not_1_out, none);
  or or_5 (out_7, all, and_10_out);
endmodule
