// Digital circuit decode_logic.dig as structural Verilog
module decode_logic (
  input  i,
  input  d2,
  input  d1,
  input  d3,
  output loadA,
  output loadD,
  output writeM
);

  wire not_1_out;

  not not_1 (not_1_out, i);
  or or_1 (loadA, not_1_out, d1);
  and and_1 (loadD, i, d2);
  and and_2 (writeM, i, d3);
endmodule
